// Logisim project Pipelined Processor Design.circ as structural Verilog: 3 circuits, main circuit main
module main (
  input  in_1,
  input  in_2,
  input  in_3,
  input  in_4,
  input  in_5,
  input  RegWrite,
  input  WBdata,
  output [7:0] out_8
);

  wire clock_1_out;
  wire [2:0] ram_1_data_2, ram_1_data_3, ram_1_data_4;
  wire [7:0] bit_extender_1_out, multiplexer_1_out, multiplexer_2_out, ram_2_data, registerfile_1_busa,
       registerfile_1_busb;
  wire [11:0] adder_1_out, PC_q;
  wire [15:0] ram_1_data;

  Adder #(.width(12)) adder_1 (.a(PC_q), .b(12'h1), .out(adder_1_out));  // open: cin, cout
  Register #(.width(12)) PC (.D(adder_1_out), .en(1'b1), .Q(PC_q), .clk(clock_1_out));  // open: clr
  Clock clock_1 (.out(clock_1_out));
  RegisterFile registerfile_1 (
    .BusW(multiplexer_2_out), .Clock(clock_1_out), .RegWrite(RegWrite), .RA(ram_1_data_2), .RB(ram_1_data_3),
    .RW(ram_1_data_4), .BusA(registerfile_1_busa), .BusB(registerfile_1_busb));
  RAM #(.addrWidth(12), .dataWidth(16)) ram_1 (
    .addr(PC_q), .data({ram_1_data[15:12], ram_1_data_4, ram_1_data_3, ram_1_data_2, ram_1_data[2:0]}),
    .clk(clock_1_out));  // open: sel, ld, clr
  Multiplexer #(.width(8), .enable("false")) multiplexer_1 (
    .in0(registerfile_1_busb), .in1(bit_extender_1_out), .out(multiplexer_1_out), .sel(in_5));
  Multiplexer #(.width(8), .enable("false")) multiplexer_2 (
    .in0(out_8), .in1(ram_2_data), .out(multiplexer_2_out), .sel(WBdata));
  assign bit_extender_1_out = {{2{ram_1_data_2[2]}}, {ram_1_data_2, ram_1_data[2:0]}};  // Bit_Extender bit_extender_1
  ALU alu_1 (
    .Op(ram_1_data[15:12]), .func(ram_1_data[2:0]), .Rt(registerfile_1_busa), .Rs(multiplexer_1_out),
    .Rd(out_8));
  RAM #(.bus("separate")) ram_2 (
    .addr(out_8), .din(registerfile_1_busb), .data(ram_2_data), .str(in_1), .sel(in_2), .clk(clock_1_out),
    .ld(in_3), .clr(in_4));

  // Notes on the sheet:
  //   Instructions Memory
  //   R-type
  //   I-Type
  //   ALUop
  //   J-type
  //   DataMemory
endmodule

module RegisterFile (
  input  [2:0] RB,
  input  [7:0] BusW,
  input  [2:0] RA,
  input  Clock,
  input  RegWrite,
  input  [2:0] RW,
  output [7:0] BusB,
  output [7:0] BusA
);

  wire _1_out, _2_out, _3_out, _4_out, _5_out, _6_out, _7_out, decoder_1_out1, decoder_1_out2,
       decoder_1_out3, decoder_1_out4, decoder_1_out5, decoder_1_out6, decoder_1_out7, decoder_2_out0,
       decoder_2_out1, decoder_2_out2, decoder_2_out3, decoder_2_out4, decoder_2_out5, decoder_2_out6,
       decoder_2_out7, decoder_3_out0, decoder_3_out1, decoder_3_out2, decoder_3_out3, decoder_3_out4,
       decoder_3_out5, decoder_3_out6, decoder_3_out7;
  wire [7:0] R1_q, R2_q, R3_q, R4_q, R5_q, R6_q, R7_q;

  Decoder #(.select(3)) decoder_1 (
    .out1(decoder_1_out1), .out2(decoder_1_out2), .out3(decoder_1_out3), .out4(decoder_1_out4),
    .out5(decoder_1_out5), .out6(decoder_1_out6), .out7(decoder_1_out7), .sel(RW), .en(1'b1));  // open: out0
  and _1 (_1_out, decoder_1_out1, RegWrite);
  and _2 (_2_out, decoder_1_out2, RegWrite);
  and _3 (_3_out, decoder_1_out3, RegWrite);
  and _4 (_4_out, decoder_1_out4, RegWrite);
  and _5 (_5_out, decoder_1_out5, RegWrite);
  and _6 (_6_out, decoder_1_out6, RegWrite);
  and _7 (_7_out, decoder_1_out7, RegWrite);
  Register R1 (.D(BusW), .en(_1_out), .Q(R1_q), .clk(Clock));  // open: clr
  Register R2 (.D(BusW), .en(_2_out), .Q(R2_q), .clk(Clock));  // open: clr
  Register R3 (.D(BusW), .en(_3_out), .Q(R3_q), .clk(Clock));  // open: clr
  Register R4 (.D(BusW), .en(_4_out), .Q(R4_q), .clk(Clock));  // open: clr
  Register R5 (.D(BusW), .en(_5_out), .Q(R5_q), .clk(Clock));  // open: clr
  Register R6 (.D(BusW), .en(_6_out), .Q(R6_q), .clk(Clock));  // open: clr
  Register R7 (.D(BusW), .en(_7_out), .Q(R7_q), .clk(Clock));  // open: clr
  assign BusA = decoder_2_out0 ? {8{1'b0}} : 8'bz;  // Controlled_Buffer controlled_buffer_1
  assign BusA = decoder_2_out2 ? R2_q : 8'bz;  // Controlled_Buffer controlled_buffer_2
  assign BusA = decoder_2_out1 ? R1_q : 8'bz;  // Controlled_Buffer controlled_buffer_3
  Decoder #(.select(3)) decoder_2 (
    .out0(decoder_2_out0), .out1(decoder_2_out1), .out2(decoder_2_out2), .out3(decoder_2_out3),
    .out4(decoder_2_out4), .out5(decoder_2_out5), .out6(decoder_2_out6), .out7(decoder_2_out7), .sel(RA),
    .en(1'b1));
  assign BusA = decoder_2_out6 ? R6_q : 8'bz;  // Controlled_Buffer controlled_buffer_4
  assign BusA = decoder_2_out5 ? R5_q : 8'bz;  // Controlled_Buffer controlled_buffer_5
  assign BusA = decoder_2_out4 ? R4_q : 8'bz;  // Controlled_Buffer controlled_buffer_6
  assign BusA = decoder_2_out3 ? R3_q : 8'bz;  // Controlled_Buffer controlled_buffer_7
  assign BusA = decoder_2_out7 ? R7_q : 8'bz;  // Controlled_Buffer controlled_buffer_8
  assign BusB = decoder_3_out0 ? {8{1'b0}} : 8'bz;  // Controlled_Buffer controlled_buffer_9
  assign BusB = decoder_3_out3 ? R3_q : 8'bz;  // Controlled_Buffer controlled_buffer_10
  assign BusB = decoder_3_out2 ? R2_q : 8'bz;  // Controlled_Buffer controlled_buffer_11
  assign BusB = decoder_3_out1 ? R1_q : 8'bz;  // Controlled_Buffer controlled_buffer_12
  Decoder #(.select(3)) decoder_3 (
    .out0(decoder_3_out0), .out1(decoder_3_out1), .out2(decoder_3_out2), .out3(decoder_3_out3),
    .out4(decoder_3_out4), .out5(decoder_3_out5), .out6(decoder_3_out6), .out7(decoder_3_out7), .sel(RB),
    .en(1'b1));
  assign BusB = decoder_3_out7 ? R7_q : 8'bz;  // Controlled_Buffer controlled_buffer_13
  assign BusB = decoder_3_out6 ? R6_q : 8'bz;  // Controlled_Buffer controlled_buffer_14
  assign BusB = decoder_3_out5 ? R5_q : 8'bz;  // Controlled_Buffer controlled_buffer_15
  assign BusB = decoder_3_out4 ? R4_q : 8'bz;  // Controlled_Buffer controlled_buffer_16

  // Notes on the sheet:
  //   STAGE 1
  //   STAGE 2
endmodule

module ALU (
  input  [3:0] Op,
  input  [2:0] func,
  input  [7:0] Rt,
  input  [7:0] Rs,
  output [7:0] Rd
);

  wire comparator_1_eq, comparator_1_gt, comparator_2_eq, comparator_2_gt, comparator_3_eq, or_2_out,
       or_3_out;
  wire [2:0] bitselector_1_out;
  wire [7:0] adder_1_out, and_1_out, and_2_out, bit_extender_1_out, bit_extender_2_out, bit_extender_3_out,
       multiplexer_1_out, multiplexer_2_out, not_1_out, not_2_out, or_1_out, shifter_1_out, shifter_2_out,
       shifter_3_out, shifter_4_out, subtractor_1_out, xor_1_out;

  BitSelector #(.group(3)) bitselector_1 (.in(Rs), .out(bitselector_1_out), .sel(2'b11));
  assign or_1_out = Rt | Rs;  // OR_Gate or_1, 8 bits wide
  assign xor_1_out = Rs ^ Rt;  // XOR_Gate xor_1, 8 bits wide
  assign and_1_out = Rs & Rt;  // AND_Gate and_1, 8 bits wide
  Adder adder_1 (.a(Rs), .b(Rt), .out(adder_1_out));  // open: cin, cout
  Subtractor subtractor_1 (.a(Rs), .b(Rt), .out(subtractor_1_out));  // open: bin, bout
  Comparator comparator_1 (.a(Rs), .b(Rt), .gt(comparator_1_gt), .eq(comparator_1_eq));  // open: lt
  Comparator #(.mode("unsigned")) comparator_2 (
    .a(Rs), .b(Rs), .gt(comparator_2_gt), .eq(comparator_2_eq));  // open: lt
  Shifter shifter_1 (.in(Rt), .\dist (bitselector_1_out), .out(shifter_1_out));
  Shifter #(.shift("ar")) shifter_2 (.in(Rt), .\dist (bitselector_1_out), .out(shifter_2_out));
  or or_2 (or_2_out, comparator_1_gt, comparator_1_eq);
  or or_3 (or_3_out, comparator_2_gt, comparator_2_eq);
  Shifter #(.shift("lr")) shifter_3 (.in(Rt), .\dist (bitselector_1_out), .out(shifter_3_out));
  Shifter #(.shift("rr")) shifter_4 (.in(Rt), .\dist (bitselector_1_out), .out(shifter_4_out));
  Comparator #(.mode("unsigned")) comparator_3 (.a(Rt), .b({8{1'b0}}), .eq(comparator_3_eq));  // open: gt, lt
  assign not_1_out = ~and_1_out;  // NOT_Gate not_1, 8 bits wide
  assign bit_extender_1_out = {{7{1'b0}}, or_2_out};  // Bit_Extender bit_extender_1
  assign bit_extender_2_out = {{7{1'b0}}, or_3_out};  // Bit_Extender bit_extender_2
  Bit_Extender #(.in_width(1), .out_width(8), .\type ("input")) bit_extender_3 (
    .in(comparator_3_eq), .out(bit_extender_3_out));  // open: extend
  assign and_2_out = bit_extender_3_out & Rs;  // AND_Gate and_2, 8 bits wide
  Multiplexer #(.select(3), .width(8), .enable("false")) multiplexer_1 (
    .in0(or_1_out), .in1(not_1_out), .in2(xor_1_out), .in4(adder_1_out), .in5(subtractor_1_out),
    .in6(bit_extender_1_out), .in7(bit_extender_2_out), .out(multiplexer_1_out), .sel(func));  // open: in3
  Multiplexer #(.select(3), .width(8), .enable("false")) multiplexer_2 (
    .in0(shifter_1_out), .in1(shifter_3_out), .in2(shifter_2_out), .in4(shifter_4_out), .in5(and_2_out),
    .in7(not_2_out), .out(multiplexer_2_out), .sel(func));  // open: in3, in6
  assign not_2_out = ~and_2_out;  // NOT_Gate not_2, 8 bits wide
  Multiplexer #(.select(4), .width(8), .enable("false")) multiplexer_3 (
    .in0(multiplexer_1_out), .in1(multiplexer_2_out), .in2(and_1_out), .in3(or_1_out), .in4(adder_1_out),
    .out(Rd), .sel(Op));  // open: in5, in6, in7, in8, in9, in10, in11, in12, in13, in14, in15

  // Notes on the sheet:
  //   ALU For Op = 0000
  //   OR 
  //   NAND
  //   XOR
  //   ADD
  //   SUB
  //   SGE
  //   SGEU
  //   ALU For Op = 0001
  //   SLL
  //   SRL
  //   SRA
  //   ROR
  //   MOVZ MOVN
  //   Signed
endmodule
